# Fritzing sketch ShieldPuzzle1v2 (saved by Fritzing 0.9.3b)
breadboards: 1

parts:
  Part1 = Arduino Uno (Rev3)
  LED1 = RGB LED (com. cathode, rgb) [package="5 mm [THT]"]
  LED2 = RGB LED (com. cathode, rgb) [package="5 mm [THT]"]
  LED3 = LED - 5mm [color="Red (633nm)" package="5 mm [THT]"]
  LED4 = LED - 5mm [color="Red (633nm)" package="5 mm [THT]"]
  LED5 = LED - 5mm [color="Red (633nm)" package="5 mm [THT]"]
  Set_Button = Pushbutton [package="[THT]"]
  S2 = Pushbutton [package="[THT]"]
  S3 = Pushbutton [package="[THT]"]
  S4 = Pushbutton [package="[THT]"]
  SW1 = DIP Switch 8 Position [package=dipswitch-08]
  J2 = Piezo Speaker
  Q2 = NPN-Transistor [package="SOT-23 [SMD]"]
  Q1 = NPN-Transistor [package="SOT-23 [SMD]"]
  Q3 = NPN-Transistor [package="SOT-23 [SMD]"]
  R1 = Resistor [tolerance=±5% resistance=220 package="0805 [SMD]"]
  R2 = Resistor [tolerance=±5% resistance=220 package="0805 [SMD]"]
  R3 = Resistor [tolerance=±5% resistance=220 package="0805 [SMD]"]
  R4 = Resistor [tolerance=±5% resistance=220 package="0805 [SMD]"]
  R5 = Resistor [tolerance=±5% resistance=220 package="0805 [SMD]"]
  R6 = Resistor [tolerance=±5% resistance=220 package="0805 [SMD]"]
  R7 = Resistor [tolerance=±5% resistance=20k package="0805 [SMD]"]
  R9 = Resistor [tolerance=±5% resistance=220 package="2010 [SMD]"]
  R10 = Resistor [tolerance=±5% resistance=220 package="2010 [SMD]"]
  R8 = Resistor [tolerance=±5% resistance=220 package="2010 [SMD]"]
  R11 = Resistor [tolerance=±5% resistance=10k package=THT]
  R12 = Resistor [tolerance=±5% resistance=10k package=THT]
  R13 = Resistor [tolerance=±5% resistance=10k package=THT]

nets:
  N1: Part1.A0, R6.Pin_0
  N2: Part1.A1, R5.Pin_0
  N3: Part1.A2, R3.Pin_0
  N4: Part1.A3, R2.Pin_0
  N5: Part1.A4/SDA, R4.Pin_0
  N6: Part1.A5/SCL, SW1.9
  N7: Part1.D8, S4.Pin_3, S4.Pin_4
  N8: Part1.D9_PWM, LED5.anode, Q1.0, R11.Pin_0
  N9: Part1.D10_PWM/SS, LED4.anode, Q2.0, R12.Pin_0
  N10: Part1.D11_PWM/MOSI, LED3.anode, Q3.0, R13.Pin_0
  N11: Part1.D12/MISO, S3.Pin_3, S3.Pin_4
  N12: Part1.D13/SCK, S2.Pin_3, S2.Pin_4, R7.Pin_0
  N13: Part1.GND, LED1.common_cathode, LED2.common_cathode, Set_Button.Pin_1, Set_Button.Pin_2, S2.Pin_1, S2.Pin_2, S3.Pin_1, S3.Pin_2, S4.Pin_1, S4.Pin_2, SW1.1, SW1.2, SW1.3, SW1.4, SW1.5, SW1.6, SW1.7, J2.pin1, R9.Pin_1, R10.Pin_1, R8.Pin_1, R11.Pin_1, R12.Pin_1, R13.Pin_1
  N14: Part1.D0/RX, SW1.10
  N15: Part1.D1/TX, SW1.11
  N16: Part1.D2, Set_Button.Pin_3, Set_Button.Pin_4
  N17: Part1.D3_PWM, SW1.12
  N18: Part1.D4, SW1.13
  N19: Part1.D5_PWM, SW1.14
  N20: Part1.D6_PWM, SW1.15
  N21: Part1.D7, SW1.16
  N22: Part1.5V, Q1.1, R7.Pin_1
  N23: LED1.red_anode, R2.Pin_1
  N24: LED1.green_anode, R4.Pin_1
  N25: LED1.blue_anode, R1.Pin_1
  N26: LED2.red_anode, R6.Pin_1
  N27: LED2.green_anode, R5.Pin_1
  N28: LED2.blue_anode, R3.Pin_1
  N29: LED3.cathode, R10.Pin_0
  N30: LED4.cathode, R9.Pin_0
  N31: LED5.cathode, R8.Pin_0
  N32: SW1.8, R1.Pin_0
  N33: J2.pin2, Q3.2
  N34: Q2.2, Q3.1
  N35: Q2.1, Q1.2

notes:
  I need to find out how many pins are required to control the 7-segment Displays.
  We could cut one Red LED and 3 dip Switches. (only 5 levels)
  When doing a first prototype, we can just use jumper cables on a breadboard instead of dip switches.
  *Dip Switch 8 is for making a temporary float to read random values

// code stored in the sketch: ShieldPuzzle1.ino
/*This is the code for my first Arduino Shield puzzle
   It will include 2 RGB LEDs
   3 Single-color LEDs
   7 buttons (6 color buttons and 1 set button) ***EDIT*** Now only 4 buttons (3 color and 1 set)
   8 dip Switches ***EDIT***Dip Switch 8 removed
   1 Beeper Buzzer ***EDIT***AND_3 with the single-color LEDs
   1  4-digit 7-segment Display ***EDIT*** Removed
 * ***EDIT*** Pull_up Pins: 12,8, 0-7, External Pull_up 13
*/
//************************************************************************************************
//Button Pins:
#define SETBUTTON 2 //interrup vector 0

#define COLORBUTTON1 13
#define COLORBUTTON2 12
#define COLORBUTTON3 8

//DipSwitch Pins:
#define DIPSWITCH1 7
#define DIPSWITCH2 6
#define DIPSWITCH3 5
#define DIPSWITCH4 4
#define DIPSWITCH5 3
#define DIPSWITCH6 0 //swapped with setbutton pin due to needed interrupt pin from pin2.
#define DIPSWITCH7 1

//Single-color LED Pins:
#define LED3 11
#define LED2 10
#define LED1 9

// RBG LED Pins:
#define SIMONRED A0
#define SIMONGREEN A1
#define SIMONBLUE A2

#define PLAYERRED A3
#define PLAYERGREEN A4
#define PLAYERBLUE A5

volatile int setButtonState = 0;         // variable for reading the pushbutton status

uint8_t Simon1 = random(1, 8); //Upper bound is exclusive
uint8_t Simon2 = random(1, 8);
uint8_t Simon3 = random(1, 8);
uint8_t Simon4 = random(1, 8);
uint8_t Simon5 = random(1, 8);
uint8_t Simon6 = random(1, 8);
uint8_t Simon7 = random(1, 8);

uint8_t Player1 = random(1, 7); //Upper bound is exclusive
uint8_t Player2 = random(1, 7);
uint8_t Player3 = random(1, 7);
uint8_t Player4 = random(1, 7);
uint8_t Player5 = random(1, 7);
uint8_t Player6 = random(1, 7);
uint8_t Player7 = random(1, 7);

 boolean b1;// These boolean values will invert the logic to be able to use active LOW as a trigger for the LEDs without confusion.
 boolean b2;
 boolean b3;

 boolean playerRedState;// Thes booleans will show which color the player LED is on regardless of that buttons were pressed.
 boolean playerGreenState;
 boolean playerBlueState;

 boolean simonRedState1;// Thes booleans will show which color the player LED is on regardless of that buttons were pressed.
 boolean simonGreenState1;
 boolean simonBlueState1;
 
 boolean simonRedState2;// Thes booleans will show which color the Simon LED is for each level regardless of what Level is currently being displayed
 boolean simonGreenState2;
 boolean simonBlueState2;

 boolean simonRedState3;
 boolean simonGreenState3;
 boolean simonBlueState3;

 boolean simonRedState4;
 boolean simonGreenState4;
 boolean simonBlueState4;

 boolean simonRedState5;
 boolean simonGreenState5;
 boolean simonBlueState5;

 boolean simonRedState6;
 boolean simonGreenState6;
 boolean simonBlueState6;

 boolean simonRedState7;
 boolean simonGreenState7;
 boolean simonBlueState7;

 boolean simonRedState8;
 boolean simonGreenState8;
 boolean simonBlueState8;

 boolean unlock1= false;// the completion states of the 7 levels.
 boolean unlock2= false;
 boolean unlock3= false;
 boolean unlock4= false;
 boolean unlock5= false;
 boolean unlock6= false;
 boolean unlock7= false;
//************************************************************************************************

void setup() {
  //Simon LED Randomized Colors:
  pinMode(PLAYERBLUE, INPUT);//temporary assignment as INPUT to read the floating value.
  randomSeed(analogRead(A5));//We are using DIPSWITCH 8 to disconnect the blue A5 input for the RGB LED and reading it as FLOAT
  pinMode(SETBUTTON, INPUT_PULLUP);

  attachInterrupt(0, pin_ISR, CHANGE);// Attach an interrupt to the ISR vector

  pinMode(COLORBUTTON1, INPUT);// cant be pulled up on Arduino, must use external pull-up.
  pinMode(COLORBUTTON2, INPUT_PULLUP);
  pinMode(COLORBUTTON3, INPUT_PULLUP);

  pinMode(DIPSWITCH7, INPUT_PULLUP);
  pinMode(DIPSWITCH6, INPUT_PULLUP);
  pinMode(DIPSWITCH5, INPUT_PULLUP);
  pinMode(DIPSWITCH4, INPUT_PULLUP);
  pinMode(DIPSWITCH3, INPUT_PULLUP);
  pinMode(DIPSWITCH2, INPUT_PULLUP);
  pinMode(DIPSWITCH1, INPUT_PULLUP);

  pinMode(LED3, OUTPUT);
  pinMode(LED2, OUTPUT);
  pinMode(LED1, OUTPUT);

  pinMode(SIMONRED, OUTPUT);
  pinMode(SIMONGREEN, OUTPUT);
  pinMode(SIMONBLUE, OUTPUT);

  pinMode(PLAYERRED, OUTPUT);
  pinMode(PLAYERGREEN, OUTPUT);
  pinMode(PLAYERBLUE, OUTPUT);
}
//************************************************************************************************

void pin_ISR() { //this function runs when the setButton is pressed
  //check the dipswitches to see what level to pass and check for.
  if (digitalRead(DIPSWITCH7)==LOW){//active low level7
    playerSelect(Player7);//turn on player LED using whatever button pattern is for level 7.
    //Check the player Red/Green/Blue states and compare to the Simon Red/Green/Blue states for each level.
    if (playerRedState==simonRedState7 && playerGreenState==simonGreenState7 && playerBlueState==simonBlueState7){
      //for testing purposes we will activate the beeper whenever a comnination is succesful.
      digitalWrite(LED3, HIGH); //111
      digitalWrite(LED2, HIGH);
      digitalWrite(LED1, HIGH);
      unlock7=true;
    }
      
  }
  else if (digitalRead(DIPSWITCH6)==LOW){
    playerSelect(Player6);
    if (playerRedState==simonRedState6 && playerGreenState==simonGreenState6 && playerBlueState==simonBlueState6){
      //for testing purposes we will activate the beeper whenever a comnination is succesful.
      digitalWrite(LED3, HIGH); //111
      digitalWrite(LED2, HIGH);
      digitalWrite(LED1, HIGH);
      unlock6=true;
    }
  }
  else if (digitalRead(DIPSWITCH5)==LOW){
    playerSelect(Player5);
    if (playerRedState==simonRedState5 && playerGreenState==simonGreenState5 && playerBlueState==simonBlueState5){
      //for testing purposes we will activate the beeper whenever a comnination is succesful.
      digitalWrite(LED3, HIGH); //111
      digitalWrite(LED2, HIGH);
      digitalWrite(LED1, HIGH);
      unlock5=true;
    }
  }
  else if (digitalRead(DIPSWITCH4)==LOW){
    playerSelect(Player4);
    if (playerRedState==simonRedState4 && playerGreenState==simonGreenState4 && playerBlueState==simonBlueState4){
      //for testing purposes we will activate the beeper whenever a comnination is succesful.
      digitalWrite(LED3, HIGH); //111
      digitalWrite(LED2, HIGH);
      digitalWrite(LED1, HIGH);
      unlock4=true;
    }
  }
  else if (digitalRead(DIPSWITCH3)==LOW){
    playerSelect(Player3);
    if (playerRedState==simonRedState3 && playerGreenState==simonGreenState3 && playerBlueState==simonBlueState3){
      //for testing purposes we will activate the beeper whenever a comnination is succesful.
      digitalWrite(LED3, HIGH); //111
      digitalWrite(LED2, HIGH);
      digitalWrite(LED1, HIGH);
      unlock3=true;
    }
  }
  else if (digitalRead(DIPSWITCH2)==LOW){
    playerSelect(Player2);
    if (playerRedState==simonRedState2 && playerGreenState==simonGreenState2 && playerBlueState==simonBlueState2){
      //for testing purposes we will activate the beeper whenever a comnination is succesful.
      digitalWrite(LED3, HIGH); //111
      digitalWrite(LED2, HIGH);
      digitalWrite(LED1, HIGH);
      unlock2=true;
    }
  }
  else if (digitalRead(DIPSWITCH1)==LOW){
    playerSelect(Player1);
    if (playerRedState==simonRedState1 && playerGreenState==simonGreenState1 && playerBlueState==simonBlueState1){
      //for testing purposes we will activate the beeper whenever a comnination is succesful.
      digitalWrite(LED3, HIGH); //111
      digitalWrite(LED2, HIGH);
      digitalWrite(LED1, HIGH);
      unlock1=true;
    }
  }
}
//************************************************************************************************
void loop() {
  if (unlock1 && unlock2 && unlock3 && unlock4 && unlock5 && unlock6 && unlock7){
    while (true){// if all of the levels are completed it will beep forever (This is just for testing).
       digitalWrite(LED3, HIGH); //111 All on should activate beep.
       digitalWrite(LED2, HIGH);
       digitalWrite(LED1, HIGH);
    }
  }
  //Level: 1
  digitalWrite(LED3, LOW); //001
  digitalWrite(LED2, LOW);
  digitalWrite(LED1, HIGH);
  simonSelect(Simon1);
  delay(1500);//Wait for 1.5 seconds

  //Level: 2
  digitalWrite(LED3, LOW); //010
  digitalWrite(LED2, HIGH);
  digitalWrite(LED1, LOW);
  simonSelect(Simon2);
  delay(1500);//Wait for 1.5 seconds

  //Level: 3
  digitalWrite(LED3, LOW); //011
  digitalWrite(LED2, HIGH);
  digitalWrite(LED1, HIGH);
  simonSelect(Simon3);
  delay(1500);//Wait for 1.5 seconds

  //Level: 4
  digitalWrite(LED3, HIGH); //100
  digitalWrite(LED2, LOW);
  digitalWrite(LED1, LOW);
  simonSelect(Simon4);
  delay(1500);//Wait for 1.5 seconds

  //Level: 5
  digitalWrite(LED3, HIGH); //101
  digitalWrite(LED2, LOW);
  digitalWrite(LED1, HIGH);
  simonSelect(Simon5);
  delay(1500);//Wait for 1.5 seconds

  //Level: 6
  digitalWrite(LED3, HIGH); //110
  digitalWrite(LED2, HIGH);
  digitalWrite(LED1, LOW);
  simonSelect(Simon6);
  delay(1500);//Wait for 1.5 seconds

  //Level: 7
  digitalWrite(LED3, HIGH); //111
  digitalWrite(LED2, HIGH);
  digitalWrite(LED1, HIGH);
  simonSelect(Simon7);
  delay(1500);//Wait for 1.5 seconds

}
//************************************************************************************************
//Displays a color combination on the Simon LED based on the value Int passed 1-7.
void simonSelect(int selectedColor) { // must be 1-7
  switch (selectedColor) {
    case 1: //BLUE
      digitalWrite(SIMONRED, LOW);
      digitalWrite(SIMONGREEN, LOW);
      digitalWrite(SIMONBLUE, HIGH);
      simonRedState1=false;
      simonGreenState1=false;
      simonBlueState1=true;
      break;
    case 2: //GREEN
      digitalWrite(SIMONRED, LOW);
      digitalWrite(SIMONGREEN, HIGH);
      digitalWrite(SIMONBLUE, LOW);
      simonRedState2=false;
      simonGreenState2=true;
      simonBlueState2=false;
      break;
    case 3: //CYAN
      digitalWrite(SIMONRED, LOW);
      digitalWrite(SIMONGREEN, HIGH);
      digitalWrite(SIMONBLUE, HIGH);
      simonRedState3=false;
      simonGreenState3=true;
      simonBlueState3=true;
      break;
    case 4: //RED
      digitalWrite(SIMONRED, HIGH);
      digitalWrite(SIMONGREEN, LOW);
      digitalWrite(SIMONBLUE, LOW);
      simonRedState4=true;
      simonGreenState4=false;
      simonBlueState4=false;
      break;
    case 5: //MAGENTA
      digitalWrite(SIMONRED, HIGH);
      digitalWrite(SIMONGREEN, LOW);
      digitalWrite(SIMONBLUE, HIGH);
      simonRedState5=true;
      simonGreenState5=false;
      simonBlueState5=true;
      break;
    case 6: //YELLOW
      digitalWrite(SIMONRED, HIGH);
      digitalWrite(SIMONGREEN, HIGH);
      digitalWrite(SIMONBLUE, LOW);
      simonRedState6=true;
      simonGreenState6=true;
      simonBlueState6=false;
      break;
    case 7: //WHITE
      digitalWrite(SIMONRED, HIGH);
      digitalWrite(SIMONGREEN, HIGH);
      digitalWrite(SIMONBLUE, HIGH);
      simonRedState7=true;
      simonGreenState7=true;
      simonBlueState7=true;
      break;
    default: //turn all OFF as default
      digitalWrite(SIMONRED, LOW);
      digitalWrite(SIMONGREEN, LOW);
      digitalWrite(SIMONBLUE, LOW);
  }
}

// this method takes a case, and activates the color of player LED based on which buttons are pressed at the time of call.
//************************************************************************************************
void playerSelect(int buttonPatternSelector) { // must be 1-6
 
  if (digitalRead(COLORBUTTON1) == LOW)// we invert the button boolean value because we are using a pulled up acctive low input.
    b1 = HIGH;
  else
    b1 = LOW;
  if (digitalRead(COLORBUTTON2) == LOW)
    b2 = HIGH;
  else
    b2 = LOW;
  if (digitalRead(COLORBUTTON3) == LOW)
    b3 = HIGH;
  else
    b3 = LOW;

  switch (buttonPatternSelector) {
    case 1: //R G B
      digitalWrite(PLAYERRED, b1);
      digitalWrite(PLAYERGREEN, b2);
      digitalWrite(PLAYERBLUE, b3);
        playerRedState=b1;
        playerGreenState=b2;
        playerBlueState=b3;
      break;
    case 2: //R B G
      digitalWrite(PLAYERRED, b1);
      digitalWrite(PLAYERBLUE, b2);
      digitalWrite(PLAYERGREEN, b3);
        playerRedState=b1;
        playerBlueState=b2;
        playerGreenState=b3;
      break;
    case 3: //G R B
      digitalWrite(PLAYERGREEN, b1);
      digitalWrite(PLAYERRED, b2);
      digitalWrite(PLAYERBLUE, b3);
        playerGreenState=b1;
        playerRedState=b2;
        playerBlueState=b3;
      break;
    case 4: //G B R
      digitalWrite(PLAYERGREEN, b1);
      digitalWrite(PLAYERBLUE, b2);
      digitalWrite(PLAYERRED, b3);
        playerGreenState=b1;
        playerBlueState=b2;
        playerRedState=b3;
      break;
    case 5: //B G R
      digitalWrite(PLAYERBLUE, b1);
      digitalWrite(PLAYERGREEN, b2);
      digitalWrite(PLAYERRED, b3);
        playerBlueState=b1;
        playerGreenState=b2;
        playerRedState=b3;
      break;
    case 6: //B R G
      digitalWrite(PLAYERBLUE, b1);
      digitalWrite(PLAYERRED, b2);
      digitalWrite(PLAYERGREEN, b3);
        playerBlueState=b1;
        playerRedState=b2;
        playerGreenState=b3;
      break;
    default: // If anything else is passed we must communicate error. For now it's just RGB with no player state booleans.
      digitalWrite(PLAYERRED, b1);
      digitalWrite(PLAYERGREEN, b2);
      digitalWrite(PLAYERBLUE, b3);
  }
}
//************************************************************************************************
